// Logisim project PC.circ as structural Verilog: 8 circuits, main circuit M
module main (
  input  in_1,
  input  in_2,
  input  in_3,
  input  in_4,
  input  [7:0] in_5,
  input  in_6,
  output [7:0] out_7
);

  R r_1 (.I(out_7), .S(in_1), .E(in_3), .O(out_7));
  enabler enabler_1 (.I(in_5), .E(in_6), .O(out_7));
  R r_2 (.I(out_7), .S(in_2), .E(in_4), .O(out_7));
endmodule

module M (
  input  I,
  input  S,
  output O
);

  wire nand_1_out, nand_2_out, nand_4_out;

  nand nand_1 (nand_1_out, I, S);
  nand nand_2 (nand_2_out, nand_1_out, S);
  nand nand_3 (O, nand_1_out, nand_4_out);
  nand nand_4 (nand_4_out, O, nand_2_out);
endmodule

module enabler (
  input  [7:0] I,
  input  E,
  output [7:0] O
);

  assign O[0] = E ? I[0] : 1'bz;  // Controlled_Buffer controlled_buffer_1
  assign O[1] = E ? I[1] : 1'bz;  // Controlled_Buffer controlled_buffer_2
  assign O[2] = E ? I[2] : 1'bz;  // Controlled_Buffer controlled_buffer_3
  assign O[3] = E ? I[3] : 1'bz;  // Controlled_Buffer controlled_buffer_4
  assign O[4] = E ? I[4] : 1'bz;  // Controlled_Buffer controlled_buffer_5
  assign O[5] = E ? I[5] : 1'bz;  // Controlled_Buffer controlled_buffer_6
  assign O[6] = E ? I[6] : 1'bz;  // Controlled_Buffer controlled_buffer_7
  assign O[7] = E ? I[7] : 1'bz;  // Controlled_Buffer controlled_buffer_8
endmodule

module B (
  input  [7:0] I,
  input  S,
  output [7:0] O
);

  M m_1 (.I(I[0]), .S(S), .O(O[0]));
  M m_2 (.I(I[1]), .S(S), .O(O[1]));
  M m_3 (.I(I[2]), .S(S), .O(O[2]));
  M m_4 (.I(I[3]), .S(S), .O(O[3]));
  M m_5 (.I(I[4]), .S(S), .O(O[4]));
  M m_6 (.I(I[5]), .S(S), .O(O[5]));
  M m_7 (.I(I[6]), .S(S), .O(O[6]));
  M m_8 (.I(I[7]), .S(S), .O(O[7]));
endmodule

module R (
  input  [7:0] I,
  input  S,
  input  E,
  output [7:0] O
);

  wire [7:0] b_1_o;

  B b_1 (.I(I), .S(S), .O(b_1_o));
  enabler enabler_1 (.I(b_1_o), .E(E), .O(O));
endmodule

module decodificador2x4 (
  input  A,
  input  B,
  output w,
  output x,
  output y,
  output z
);

  wire nand_1_out, nand_2_out, nand_3_out, nand_4_out, nand_5_out, nand_7_out, nand_9_out, nand_11_out;

  nand nand_1 (nand_1_out, A, A);
  nand nand_2 (nand_2_out, B, B);
  nand nand_3 (nand_3_out, A, A);
  nand nand_4 (nand_4_out, B, B);
  nand nand_5 (nand_5_out, nand_1_out, nand_2_out);
  nand nand_6 (w, nand_5_out, nand_5_out);
  nand nand_7 (nand_7_out, nand_3_out, B);
  nand nand_8 (x, nand_7_out, nand_7_out);
  nand nand_9 (nand_9_out, A, nand_4_out);
  nand nand_10 (y, nand_9_out, nand_9_out);
  nand nand_11 (nand_11_out, A, B);
  nand nand_12 (z, nand_11_out, nand_11_out);

  // Notes on the sheet:
  //   E possivel usar not no lugar de nand para deixar o circuito mais simples,
  //   mas na implementacao utilizando somente portas nand, e assim que faz
endmodule

module celula (
  input  [7:0] I,
  input  C,
  input  L,
  input  S,
  input  E,
  output [7:0] O
);

  wire nand_1_out, nand_2_out, nand_3_out, nand_4_out, nand_5_out, nand_6_out;

  nand nand_1 (nand_1_out, C, L);
  nand nand_2 (nand_2_out, nand_1_out, nand_1_out);
  nand nand_3 (nand_3_out, nand_2_out, S);
  nand nand_4 (nand_4_out, nand_2_out, E);
  nand nand_5 (nand_5_out, nand_3_out, nand_3_out);
  nand nand_6 (nand_6_out, nand_4_out, nand_4_out);
  R r_1 (.I(I), .S(nand_5_out), .E(nand_6_out), .O(O));
endmodule

module RAM1 (
  input  [7:0] in_1,
  input  in_2,
  input  [7:0] in_3,
  input  S,
  input  in_5,
  input  E,
  input  in_7,
  output [7:0] out_8
);

  wire decodificador2x4_1_w, decodificador2x4_1_x, decodificador2x4_1_y, decodificador2x4_1_z,
       decodificador2x4_2_w, decodificador2x4_2_x, decodificador2x4_2_y, decodificador2x4_2_z;
  wire [7:0] MAR_o;

  R MAR (.I(in_1), .S(in_2), .E(1'b1), .O(MAR_o));
  R r_1 (.I(in_3), .S(in_5), .E(in_7), .O(out_8));
  decodificador2x4 decodificador2x4_1 (
    .A(MAR_o[0]), .B(MAR_o[1]), .w(decodificador2x4_1_w), .x(decodificador2x4_1_x), .y(decodificador2x4_1_y),
    .z(decodificador2x4_1_z));
  decodificador2x4 decodificador2x4_2 (
    .A(MAR_o[2]), .B(MAR_o[3]), .w(decodificador2x4_2_w), .x(decodificador2x4_2_x), .y(decodificador2x4_2_y),
    .z(decodificador2x4_2_z));
  celula celula_1 (.I(out_8), .C(decodificador2x4_2_w), .L(decodificador2x4_1_w), .S(S), .E(E), .O(out_8));
  celula celula_2 (.I(out_8), .C(decodificador2x4_2_w), .L(decodificador2x4_1_x), .S(S), .E(E), .O(out_8));
  celula celula_3 (.I(out_8), .C(decodificador2x4_2_w), .L(decodificador2x4_1_y), .S(S), .E(E), .O(out_8));
  celula celula_4 (.I(out_8), .C(decodificador2x4_2_w), .L(decodificador2x4_1_z), .S(S), .E(E), .O(out_8));
  celula celula_5 (.I(out_8), .C(decodificador2x4_2_x), .L(decodificador2x4_1_w), .S(S), .E(E), .O(out_8));
  celula celula_6 (.I(out_8), .C(decodificador2x4_2_x), .L(decodificador2x4_1_x), .S(S), .E(E), .O(out_8));
  celula celula_7 (.I(out_8), .C(decodificador2x4_2_x), .L(decodificador2x4_1_y), .S(S), .E(E), .O(out_8));
  celula celula_8 (.I(out_8), .C(decodificador2x4_2_x), .L(decodificador2x4_1_z), .S(S), .E(E), .O(out_8));
  celula celula_9 (.I(out_8), .C(decodificador2x4_2_y), .L(decodificador2x4_1_w), .S(S), .E(E), .O(out_8));
  celula celula_10 (.I(out_8), .C(decodificador2x4_2_y), .L(decodificador2x4_1_x), .S(S), .E(E), .O(out_8));
  celula celula_11 (.I(out_8), .C(decodificador2x4_2_y), .L(decodificador2x4_1_y), .S(S), .E(E), .O(out_8));
  celula celula_12 (.I(out_8), .C(decodificador2x4_2_y), .L(decodificador2x4_1_z), .S(S), .E(E), .O(out_8));
  celula celula_13 (.I(out_8), .C(decodificador2x4_2_z), .L(decodificador2x4_1_w), .S(S), .E(E), .O(out_8));
  celula celula_14 (.I(out_8), .C(decodificador2x4_2_z), .L(decodificador2x4_1_x), .S(S), .E(E), .O(out_8));
  celula celula_15 (.I(out_8), .C(decodificador2x4_2_z), .L(decodificador2x4_1_y), .S(S), .E(E), .O(out_8));
  celula celula_16 (.I(out_8), .C(decodificador2x4_2_z), .L(decodificador2x4_1_z), .S(S), .E(E), .O(out_8));
endmodule
